# Fritzing sketch Car (saved by Fritzing 0.9.4)

parts:
  L298N1 = L298N DC motor driver
  元件1 = Arduino Mega 2560 (Rev3)
  L298N2 = L298N DC motor driver
  元件2 = Bluetooth HC-05 Macho
  J1 = Basic Servo
  M1 = 5-ir-array-sensor [package=THT]
  VCC1 = Battery block 9V
  HC-SR04_Sensor_1 = HC-SR04 Ultrasonic Distance Sensor
  M2 = DC Motor  # not connected
  M3 = DC Motor  # not connected
  M4 = DC Motor  # not connected
  M5 = DC Motor  # not connected
  LED1 = LED - 5mm [color="Red (633nm)" package="5 mm [THT]"]  # not connected
  R2 = Resistor [tolerance=±5% resistance=220 package=THT]
  LED2 = smd LED [color="Red (633nm)" package="0805 [SMD]"]
  R3 = Resistor [tolerance=±5% resistance=220 package=THT]

nets:
  12V: L298N1.12V, L298N2.12V, VCC1.+
  N1: L298N1.GND, VCC1.-
  N2: L298N1.ENA, L298N1.IN1, 元件1.D12_PWM
  N3: L298N1.IN2, 元件1.D11_PWM
  N4: L298N1.IN3, 元件1.D10_PWM
  N5: L298N1.IN4, 元件1.D9_PWM
  N6: 元件1.A0, M1.S5
  N7: 元件1.A1, M1.S4
  N8: 元件1.A2, M1.S3
  N9: 元件1.A3, M1.S2
  N10: 元件1.A4, M1.S1
  N11: 元件1.D15/RX3, 元件2.TXD
  N12: 元件1.D14/TX3, 元件2.RXD
  N13: 元件1.D8_PWM, L298N2.IN1
  5V: 元件1.5V, L298N2.5V, HC-SR04_Sensor_1.VCC
  GND: 元件1.GND, HC-SR04_Sensor_1.GND
  N14: 元件1.D5_PWM, L298N2.IN4
  N15: 元件1.D6_PWM, L298N2.IN3
  N16: 元件1.D7_PWM, L298N2.IN2
  N17: 元件1.D49, R3.Pin_0
  N18: 元件1.D50, HC-SR04_Sensor_1.TRIG
  N19: 元件1.D51, HC-SR04_Sensor_1.ECHO
  N20: 元件1.D52, R2.Pin_0
  N21: 元件1.D53, J1.pulse
  N22: L298N2.GND, LED2.cathode

custom parts:
  L298N DC motor driver: 2x DC motor driver with 78M05 positive voltage regulator (7..35 V) L298N: max 46 V, 2 A Set 5 V Enable jumper to enable 5 V regultor (needed for the L298N) and +5 V output at screw terminal or supply external +5 V at screw terminal Set ENA and/or ENB to +5 V to enable motor permanently or supply ENA and/or ENB with PWM signal IN1 and IN2 set rotation directory for motor A (OUT1/OUT2) IN2 and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
  5-ir-array-sensor: 5 IR array sensor.
